// Logisim project cpu2.circ as structural Verilog: 5 circuits, main circuit main
module main (
  input  [31:0] INSTRUCTION,
  input  CLOCK,
  output [31:0] FETCH_ADDRESS,
  output [31:0] ra,
  output [31:0] sp,
  output [31:0] t0,
  output [31:0] t1,
  output [31:0] t2,
  output [31:0] s0,
  output [31:0] s1,
  output [31:0] a0
);

  wire branchcomp_1_breq, branchcomp_1_brlt, controlla_1_brun, controlla_1_bsel, controlla_1_memrw,
       controlla_1_pcsel, controlla_1_regwen, controlla_1_spsel;
  wire [1:0] controlla_1_asel, controlla_1_funct3_load, controlla_1_wbsel;
  wire [2:0] controlla_1_immsel;
  wire [3:0] controlla_1_alusel;
  wire [4:0] chosen_rd, rd;
  wire [31:0] adder_1_out, adder_2_out, ALU, DMEM_p5, immediategen_1_imm_result, INSTRUCTION_t,
       loadgen_1_load_result, multiplexer_1_out, multiplexer_4_out, multiplexer_5_out, PC, PROGRAM_COUNTER,
       RegFile_read_data_1, RegFile_read_data_2, register_2_q, WriteBack;

  Adder #(.width(32)) adder_1 (.a(PROGRAM_COUNTER), .b(32'h4), .out(adder_1_out));  // open: cin, cout
  Multiplexer #(.width(32), .enable("false")) multiplexer_1 (
    .in0(adder_1_out), .in1(ALU), .out(multiplexer_1_out), .sel(controlla_1_pcsel));
  Register #(.width(32)) u_PC (.D(multiplexer_1_out), .clk(CLOCK), .Q(PROGRAM_COUNTER));  // open: en, clr
  Shifter #(.width(32), .shift("lr")) shifter_1 (.in(PROGRAM_COUNTER), .\dist (5'b00010), .out(FETCH_ADDRESS));
  Register #(.width(32)) register_1 (.D(PROGRAM_COUNTER), .clk(CLOCK), .Q(PC));  // open: en, clr
  Register #(.width(32)) register_2 (
    .D(INSTRUCTION_t), .clk(CLOCK), .Q({register_2_q[31:12], rd, register_2_q[6:0]}));  // open: en, clr
  Multiplexer #(.width(32), .enable("false")) multiplexer_2 (
    .in0(INSTRUCTION), .in1(32'h13), .out(INSTRUCTION_t), .sel(controlla_1_pcsel));
  Controlla controlla_1 (
    .Instruction({register_2_q[31:12], rd, register_2_q[6:0]}), .BrEQ(branchcomp_1_breq),
    .BrLT(branchcomp_1_brlt), .RS2(RegFile_read_data_2), .PCSel(controlla_1_pcsel),
    .RegWEn(controlla_1_regwen), .ImmSel(controlla_1_immsel), .ASel(controlla_1_asel),
    .BSel(controlla_1_bsel), .ALUSel(controlla_1_alusel), .MemRW(controlla_1_memrw),
    .WBSel(controlla_1_wbsel), .BrUn(controlla_1_brun), .SPSel(controlla_1_spsel),
    .Funct3_load(controlla_1_funct3_load));
  ImmediateGen immediategen_1 (
    .Instruction({register_2_q[31:12], rd, register_2_q[6:0]}), .ImmSel(controlla_1_immsel),
    .Imm_Result(immediategen_1_imm_result));
  Multiplexer #(.width(5), .enable("false")) multiplexer_3 (
    .in0(5'b00010), .in1(rd), .out(chosen_rd), .sel(controlla_1_spsel));
  regfile_main RegFile (
    .rs2(register_2_q[24:20]), .rd(chosen_rd), .Read_Data_1(RegFile_read_data_1),
    .Read_Data_2(RegFile_read_data_2), .ra(ra), .sp(sp), .t0(t0), .t1(t1), .t2(t2), .s0(s0), .s1(s1),
    .a0(a0), .rs1(register_2_q[19:15]), .Write_Data(WriteBack), .RegWEn(controlla_1_regwen), .clk(CLOCK));
  BranchComp branchcomp_1 (
    .br_r1(RegFile_read_data_1), .br_r2(RegFile_read_data_2), .in_3(controlla_1_brun),
    .BrEQ(branchcomp_1_breq), .BrLT(branchcomp_1_brlt));
  Multiplexer #(.select(2), .width(32), .enable("false")) multiplexer_4 (
    .in0(RegFile_read_data_1), .in1(PC), .in2(sp), .out(multiplexer_4_out), .sel(controlla_1_asel));  // open: in3
  Multiplexer #(.width(32), .enable("false")) multiplexer_5 (
    .in0(RegFile_read_data_2), .in1(immediategen_1_imm_result), .out(multiplexer_5_out),
    .sel(controlla_1_bsel));
  alu Arithmetic_Logic_Unit (.A(multiplexer_4_out), .B(multiplexer_5_out), .ALUSel(controlla_1_alusel), .Result(ALU));
  Adder #(.width(32)) adder_2 (.a(32'h4), .b(PC), .out(adder_2_out));  // open: cin, cout
  // mem_main DMEM: pin names not known; wires that end beside it: ALU, RegFile_read_data_2, controlla_1_memrw, CLOCK, DMEM_p5
  LoadGen loadgen_1 (
    .Load_Bits(ALU), .ReadData(DMEM_p5), .LoadSel(controlla_1_funct3_load),
    .Load_Result(loadgen_1_load_result));
  Multiplexer #(.select(2), .width(32), .enable("false")) multiplexer_6 (
    .in0(adder_2_out), .in1(ALU), .in2(loadgen_1_load_result), .out(WriteBack), .sel(controlla_1_wbsel));  // open: in3

  // Other names for the same wires on the sheet: clk = CLOCK

  // Notes on the sheet:
  //   Output
  //   Inputs/Outputs from run.circ. DO NOT MOVE THESE.
  //   Inputs
  //   It is OK to move the PC, RegFile, ALU, and MEM to wherever is most convenient for you when constructing your CPU, and to delete this text
  //   Inputs/Outputs from run.circ. DO NOT MOVE THESE.
endmodule

module ImmediateGen (
  input  [31:0] Instruction,
  input  [2:0] ImmSel,
  output [31:0] Imm_Result
);

  wire [31:0] LWC_Type, shifter_1_out, U_Type;
  wire [31:11] I_Type, S_Type;
  wire [31:12] B_Type;
  wire [31:20] J_Type;

  assign B_Type = {{19{Instruction[31]}}, Instruction[31]};  // Bit_Extender bit_extender_1
  Shifter #(.width(32), .shift("lr")) shifter_1 (.in(Instruction), .\dist (5'b01100), .out(shifter_1_out));
  assign J_Type = {{11{Instruction[31]}}, Instruction[31]};  // Bit_Extender bit_extender_2
  assign LWC_Type = {{25{Instruction[31]}}, Instruction[31:25]};  // Bit_Extender bit_extender_3
  assign I_Type = {{20{Instruction[31]}}, Instruction[31]};  // Bit_Extender bit_extender_4
  assign S_Type = {{20{Instruction[31]}}, Instruction[31]};  // Bit_Extender bit_extender_5
  Shifter #(.width(32)) shifter_2 (.in(shifter_1_out), .\dist (5'b01100), .out(U_Type));
  Multiplexer #(.select(3), .width(32), .enable("false")) multiplexer_1 (
    .in0({I_Type, Instruction[30:20]}), .in1({S_Type, Instruction[30:25], Instruction[11:7]}),
    .in2({B_Type, Instruction[7], Instruction[30:25], Instruction[11:8], 1'b0}), .in3(U_Type),
    .in4({J_Type, Instruction[19:12], Instruction[20], Instruction[30:21], Instruction[0]}), .in5(LWC_Type),
    .in6(32'h4), .out(Imm_Result), .sel(ImmSel));  // open: in7

  // Other names for the same wires on the sheet: B_Type[11:1] = {Instruction[7], Instruction[30:25], Instruction[11:8]};
  //   Immediate[31:0] = Instruction; S_Type[10:0] = {Instruction[30:25], Instruction[11:7]};
  //   J_Type[19:0] = {Instruction[19:12], Instruction[20], Instruction[30:21], Instruction[0]};
  //   I_Type[10:0] = Instruction[30:20]

  // Notes on the sheet:
  //   Inputs
  //   Output
endmodule

module Controlla (
  input  [31:0] Instruction,
  input  BrEQ,
  input  BrLT,
  input  [31:0] RS2,
  output PCSel,
  output RegWEn,
  output [2:0] ImmSel,
  output [1:0] ASel,
  output BSel,
  output [3:0] ALUSel,
  output MemRW,
  output [1:0] WBSel,
  output BrUn,
  output SPSel,
  output [1:0] Funct3_load
);

  wire add, addi, and_1, and_1_out, and_2_out, and_3_out, and_4_out, and_5_out, and_6_out, and_7_out,
       and_8_out, and_9_out, and_10_out, and_11_out, and_12_out, and_45_out, and_48_out, andi, beq, blt, bne,
       comparator_1_eq, comparator_2_eq, comparator_3_eq, comparator_4_eq, comparator_4_gt, comparator_5_eq,
       comparator_6_eq, comparator_7_eq, comparator_8_eq, comparator_10_eq, comparator_11_eq,
       comparator_12_eq, comparator_13_eq, comparator_14_eq, comparator_15_eq, comparator_16_eq,
       comparator_19_eq, comparator_20_eq, comparator_21_eq, comparator_22_eq, comparator_23_eq,
       comparator_24_eq, comparator_25_eq, comparator_27_eq, comparator_28_eq, comparator_30_eq,
       comparator_31_eq, comparator_34_eq, comparator_35_eq, comparator_36_eq, comparator_37_eq,
       comparator_38_eq, comparator_39_eq, divu, I_load, I_not_load, jal, jalr, lb, lh, lui, lw, lwc, mul,
       mulh, mulhu, not_1_out, or_1, or_1_out, or_3_out, or_4_out, or_5_out, or_8_out, or_9_out, or_10_out,
       or_14_out, or_15_out, or_16_out, or_17_out, or_18_out, or_19_out, or_20_out, or_21_out, or_22_out,
       ori, pop, push, push_or_pop, R_type, remu, rs2_is_0, SB_Type, sll_1, slli, slt, slti, sra_1, srai,
       srl_1, srli, sub, sw, xor_1, xori;
  wire [1:0] and_13_out, and_14_out, and_15_out, and_30_out, and_31_out, and_32_out, bit_extender_1_out,
       bit_extender_2_out, bit_extender_3_out, bit_extender_4_out, bit_extender_5_out, bit_extender_6_out;
  wire [2:0] and_33_out, and_34_out, and_35_out, and_36_out, and_37_out, and_38_out, and_39_out,
       bit_extender_7_out, bit_extender_8_out, bit_extender_9_out, bit_extender_10_out, bit_extender_11_out,
       bit_extender_12_out, bit_extender_13_out;
  wire [3:0] and_51_out, and_52_out, and_53_out, and_54_out, and_55_out, and_56_out, and_57_out, and_58_out,
       and_59_out, and_60_out, and_61_out, and_62_out, and_63_out, and_64_out, and_65_out,
       bit_extender_14_out, bit_extender_15_out, bit_extender_16_out, bit_extender_17_out,
       bit_extender_18_out, bit_extender_19_out, bit_extender_20_out, bit_extender_21_out,
       bit_extender_22_out, bit_extender_23_out, bit_extender_24_out, bit_extender_25_out,
       bit_extender_26_out, bit_extender_27_out, bit_extender_28_out;

  Comparator #(.width(3)) comparator_1 (.a(Instruction[14:12]), .b(3'b000), .eq(comparator_1_eq));  // open: gt, lt
  Comparator #(.width(3)) comparator_2 (.a(Instruction[14:12]), .b(3'b001), .eq(comparator_2_eq));  // open: gt, lt
  Comparator #(.width(3)) comparator_3 (.a(Instruction[14:12]), .b(3'b010), .eq(comparator_3_eq));  // open: gt, lt
  Comparator #(.width(3)) comparator_4 (
    .a(Instruction[14:12]), .b(3'b011), .gt(comparator_4_gt), .eq(comparator_4_eq));  // open: lt
  Comparator #(.width(3)) comparator_5 (.a(Instruction[14:12]), .b(3'b100), .eq(comparator_5_eq));  // open: gt, lt
  Comparator #(.width(3)) comparator_6 (.a(Instruction[14:12]), .b(3'b101), .eq(comparator_6_eq));  // open: gt, lt
  Comparator #(.width(3)) comparator_7 (.a(Instruction[14:12]), .b(3'b110), .eq(comparator_7_eq));  // open: gt, lt
  Comparator #(.width(3)) comparator_8 (.a(Instruction[14:12]), .b(3'b111), .eq(comparator_8_eq));  // open: gt, lt
  Comparator #(.width(7)) comparator_9 (.a(Instruction[6:0]), .b(7'b0110011), .eq(R_type));  // open: gt, lt
  and u_and_1 (and_1_out, rs2_is_0, lwc);
  not not_1 (not_1_out, BrEQ);
  or u_or_1 (or_1_out, blt, BrUn);
  or or_2 (MemRW, sw, push);
  Comparator #(.width(7)) comparator_10 (
    .a(Instruction[31:25]), .b(7'b0100000), .eq(comparator_10_eq));  // open: gt, lt
  Comparator #(.width(7)) comparator_11 (
    .a(Instruction[31:25]), .b(7'b0000001), .eq(comparator_11_eq));  // open: gt, lt
  Comparator #(.width(7)) comparator_12 (.a(Instruction[31:25]), .b({7{1'b0}}), .eq(comparator_12_eq));  // open: gt, lt
  and and_2 (and_2_out, bne, not_1_out);
  and and_3 (and_3_out, beq, BrEQ);
  and and_4 (and_4_out, or_1_out, BrLT);
  or or_3 (or_3_out, jalr, jal);
  or or_4 (or_4_out, R_type, lui, push_or_pop, I_not_load);
  assign bit_extender_1_out = {{1{or_5_out}}, or_5_out};  // Bit_Extender bit_extender_1
  or or_5 (or_5_out, I_load, lwc);
  and and_5 (and_5_out, comparator_1_eq, R_type);
  and and_6 (and_6_out, comparator_2_eq, R_type);
  and and_7 (and_7_out, comparator_3_eq, R_type);
  and and_8 (and_8_out, comparator_4_eq, R_type);
  and and_9 (and_9_out, comparator_5_eq, R_type);
  and and_10 (and_10_out, comparator_6_eq, R_type);
  and and_11 (and_11_out, comparator_7_eq, R_type);
  and and_12 (and_12_out, comparator_8_eq, R_type);
  or or_6 (PCSel, jalr, jal, and_2_out, and_3_out, and_4_out);
  nor nor_1 (RegWEn, SB_Type, and_1_out, sw);
  assign bit_extender_2_out = {{1{or_3_out}}, or_3_out};  // Bit_Extender bit_extender_2
  assign bit_extender_3_out = {{1{or_4_out}}, or_4_out};  // Bit_Extender bit_extender_3
  assign and_13_out = bit_extender_2_out & 2'b00;  // AND_Gate and_13, 2 bits wide
  assign and_14_out = bit_extender_3_out & 2'b01;  // AND_Gate and_14, 2 bits wide
  assign and_15_out = bit_extender_1_out & 2'b10;  // AND_Gate and_15, 2 bits wide
  assign WBSel = and_13_out | and_14_out | and_15_out;  // OR_Gate or_7, 2 bits wide
  or or_8 (or_8_out, R_type, I_not_load, I_load, sw, lui, jal);
  or or_9 (or_9_out, SB_Type, jal);
  and and_16 (sub, comparator_10_eq, and_5_out);
  and and_17 (mul, comparator_11_eq, and_5_out);
  and and_18 (add, comparator_12_eq, and_5_out);
  and and_19 (sll_1, comparator_12_eq, and_6_out);
  and and_20 (mulh, comparator_11_eq, and_6_out);
  and and_21 (slt, comparator_12_eq, and_7_out);
  and and_22 (mulhu, comparator_11_eq, and_8_out);
  and and_23 (xor_1, comparator_12_eq, and_9_out);
  and and_24 (srl_1, comparator_12_eq, and_10_out);
  and and_25 (divu, comparator_11_eq, and_10_out);
  and and_26 (sra_1, comparator_10_eq, and_10_out);
  and and_27 (or_1, comparator_12_eq, and_11_out);
  and and_28 (remu, comparator_11_eq, and_12_out);
  and and_29 (and_1, comparator_12_eq, and_12_out);
  assign bit_extender_4_out = {{1{or_8_out}}, or_8_out};  // Bit_Extender bit_extender_4
  assign bit_extender_5_out = {{1{or_9_out}}, or_9_out};  // Bit_Extender bit_extender_5
  assign bit_extender_6_out = {{1{push_or_pop}}, push_or_pop};  // Bit_Extender bit_extender_6
  assign bit_extender_7_out = {{2{or_10_out}}, or_10_out};  // Bit_Extender bit_extender_7
  or or_10 (or_10_out, I_load, jalr, pop, I_not_load);
  assign bit_extender_8_out = {{2{sw}}, sw};  // Bit_Extender bit_extender_8
  assign bit_extender_9_out = {{2{SB_Type}}, SB_Type};  // Bit_Extender bit_extender_9
  assign bit_extender_10_out = {{2{lui}}, lui};  // Bit_Extender bit_extender_10
  assign bit_extender_11_out = {{2{jal}}, jal};  // Bit_Extender bit_extender_11
  assign bit_extender_12_out = {{2{lwc}}, lwc};  // Bit_Extender bit_extender_12
  assign bit_extender_13_out = {{2{push}}, push};  // Bit_Extender bit_extender_13
  assign and_30_out = bit_extender_4_out & 2'b00;  // AND_Gate and_30, 2 bits wide
  assign and_31_out = bit_extender_5_out & 2'b01;  // AND_Gate and_31, 2 bits wide
  assign and_32_out = bit_extender_6_out & 2'b10;  // AND_Gate and_32, 2 bits wide
  or or_11 (BSel, I_load, I_not_load, sw, push_or_pop, SB_Type, lui, jal);
  assign and_33_out = bit_extender_7_out & 3'b000;  // AND_Gate and_33, 3 bits wide
  assign and_34_out = bit_extender_8_out & 3'b001;  // AND_Gate and_34, 3 bits wide
  assign and_35_out = bit_extender_9_out & 3'b010;  // AND_Gate and_35, 3 bits wide
  assign and_36_out = bit_extender_10_out & 3'b011;  // AND_Gate and_36, 3 bits wide
  assign and_37_out = bit_extender_11_out & 3'b100;  // AND_Gate and_37, 3 bits wide
  assign and_38_out = bit_extender_12_out & 3'b101;  // AND_Gate and_38, 3 bits wide
  assign and_39_out = bit_extender_13_out & 3'b110;  // AND_Gate and_39, 3 bits wide
  assign ASel = and_30_out | and_31_out | and_32_out;  // OR_Gate or_12, 2 bits wide
  Comparator #(.width(3)) comparator_13 (.a(Instruction[14:12]), .b(3'b100), .eq(comparator_13_eq));  // open: gt, lt
  Comparator #(.width(3)) comparator_14 (.a(Instruction[14:12]), .b(3'b101), .eq(comparator_14_eq));  // open: gt, lt
  Comparator #(.width(3)) comparator_15 (.a(Instruction[14:12]), .b(3'b110), .eq(comparator_15_eq));  // open: gt, lt
  Comparator #(.width(3)) comparator_16 (.a(Instruction[14:12]), .b(3'b111), .eq(comparator_16_eq));  // open: gt, lt
  Comparator #(.width(7)) comparator_17 (.a(Instruction[6:0]), .b(7'b0000011), .eq(I_load));  // open: gt, lt
  Comparator #(.width(7)) comparator_18 (.a(Instruction[6:0]), .b(7'b0010011), .eq(I_not_load));  // open: gt, lt
  assign ImmSel = and_33_out | and_34_out | and_35_out | and_36_out | and_37_out | and_38_out | and_39_out;  // OR_Gate or_13, 3 bits wide
  Comparator #(.width(3)) comparator_19 (.a(Instruction[14:12]), .b(3'b111), .eq(comparator_19_eq));  // open: gt, lt
  Comparator #(.width(7)) comparator_20 (.a(Instruction[6:0]), .b(7'b0000011), .eq(comparator_20_eq));  // open: gt, lt
  Comparator #(.width(3)) comparator_21 (.a(Instruction[14:12]), .b(3'b000), .eq(comparator_21_eq));  // open: gt, lt
  Comparator #(.width(3)) comparator_22 (.a(Instruction[14:12]), .b(3'b001), .eq(comparator_22_eq));  // open: gt, lt
  Comparator #(.width(3)) comparator_23 (.a(Instruction[14:12]), .b(3'b010), .eq(comparator_23_eq));  // open: gt, lt
  and and_40 (lwc, comparator_19_eq, comparator_20_eq);
  or or_14 (or_14_out, lwc, addi, add, SB_Type, jal, jalr, sw, I_load, pop);
  and and_41 (lb, comparator_21_eq, I_load);
  and and_42 (lh, comparator_22_eq, I_load);
  and and_43 (lw, comparator_23_eq, I_load);
  and and_44 (addi, comparator_21_eq, I_not_load);
  and and_45 (and_45_out, comparator_22_eq, I_not_load);
  and and_46 (slti, comparator_23_eq, I_not_load);
  and and_47 (xori, comparator_13_eq, I_not_load);
  and and_48 (and_48_out, comparator_14_eq, I_not_load);
  and and_49 (ori, comparator_15_eq, I_not_load);
  and and_50 (andi, comparator_16_eq, I_not_load);
  or or_15 (or_15_out, and_1, andi);
  or or_16 (or_16_out, or_1, ori);
  or or_17 (or_17_out, xor_1, xori);
  or or_18 (or_18_out, srl_1, srli);
  or or_19 (or_19_out, sra_1, srai);
  or or_20 (or_20_out, sll_1, slli);
  or or_21 (or_21_out, slt, slti);
  or or_22 (or_22_out, sub, push);
  assign bit_extender_14_out = {{3{or_14_out}}, or_14_out};  // Bit_Extender bit_extender_14
  assign bit_extender_15_out = {{3{or_15_out}}, or_15_out};  // Bit_Extender bit_extender_15
  assign bit_extender_16_out = {{3{or_16_out}}, or_16_out};  // Bit_Extender bit_extender_16
  assign bit_extender_17_out = {{3{or_17_out}}, or_17_out};  // Bit_Extender bit_extender_17
  assign bit_extender_18_out = {{3{or_18_out}}, or_18_out};  // Bit_Extender bit_extender_18
  assign bit_extender_19_out = {{3{or_19_out}}, or_19_out};  // Bit_Extender bit_extender_19
  assign bit_extender_20_out = {{3{or_20_out}}, or_20_out};  // Bit_Extender bit_extender_20
  assign bit_extender_21_out = {{3{or_21_out}}, or_21_out};  // Bit_Extender bit_extender_21
  assign bit_extender_22_out = {{3{divu}}, divu};  // Bit_Extender bit_extender_22
  assign bit_extender_23_out = {{3{remu}}, remu};  // Bit_Extender bit_extender_23
  assign bit_extender_24_out = {{3{mul}}, mul};  // Bit_Extender bit_extender_24
  assign bit_extender_25_out = {{3{mulhu}}, mulhu};  // Bit_Extender bit_extender_25
  assign bit_extender_26_out = {{3{or_22_out}}, or_22_out};  // Bit_Extender bit_extender_26
  assign bit_extender_27_out = {{3{lui}}, lui};  // Bit_Extender bit_extender_27
  assign bit_extender_28_out = {{3{mulh}}, mulh};  // Bit_Extender bit_extender_28
  Comparator #(.width(3)) comparator_24 (.a(Instruction[14:12]), .b(3'b011), .eq(comparator_24_eq));  // open: gt, lt
  Comparator #(.width(3)) comparator_25 (.a(Instruction[14:12]), .b(3'b010), .eq(comparator_25_eq));  // open: gt, lt
  Comparator #(.width(7)) comparator_26 (.a(Instruction[6:0]), .b(7'b0111011), .eq(push_or_pop));  // open: gt, lt
  Comparator #(.width(7)) comparator_27 (.a(Instruction[31:25]), .b({7{1'b0}}), .eq(comparator_27_eq));  // open: gt, lt
  assign and_51_out = bit_extender_14_out & 4'b0000;  // AND_Gate and_51, 4 bits wide
  assign and_52_out = bit_extender_15_out & 4'b0001;  // AND_Gate and_52, 4 bits wide
  assign and_53_out = bit_extender_16_out & 4'b0010;  // AND_Gate and_53, 4 bits wide
  assign and_54_out = bit_extender_17_out & 4'b0011;  // AND_Gate and_54, 4 bits wide
  assign and_55_out = bit_extender_18_out & 4'b0100;  // AND_Gate and_55, 4 bits wide
  assign and_56_out = bit_extender_19_out & 4'b0101;  // AND_Gate and_56, 4 bits wide
  assign and_57_out = bit_extender_20_out & 4'b0110;  // AND_Gate and_57, 4 bits wide
  assign and_58_out = bit_extender_21_out & 4'b0111;  // AND_Gate and_58, 4 bits wide
  assign and_59_out = bit_extender_22_out & 4'b1000;  // AND_Gate and_59, 4 bits wide
  assign and_60_out = bit_extender_23_out & 4'b1001;  // AND_Gate and_60, 4 bits wide
  assign and_61_out = bit_extender_24_out & 4'b1010;  // AND_Gate and_61, 4 bits wide
  assign and_62_out = bit_extender_25_out & 4'b1011;  // AND_Gate and_62, 4 bits wide
  assign and_63_out = bit_extender_26_out & 4'b1100;  // AND_Gate and_63, 4 bits wide
  assign and_64_out = bit_extender_27_out & 4'b1101;  // AND_Gate and_64, 4 bits wide
  assign and_65_out = bit_extender_28_out & 4'b1110;  // AND_Gate and_65, 4 bits wide
  and and_66 (push, comparator_24_eq, push_or_pop);
  and and_67 (pop, comparator_25_eq, push_or_pop);
  Comparator #(.width(7)) comparator_28 (
    .a(Instruction[31:25]), .b(7'b0100000), .eq(comparator_28_eq));  // open: gt, lt
  and and_68 (slli, comparator_27_eq, and_45_out);
  and and_69 (srli, comparator_27_eq, and_48_out);
  and and_70 (srai, comparator_28_eq, and_48_out);
  assign ALUSel = and_51_out | and_52_out | and_53_out | and_54_out | and_55_out | and_56_out | and_57_out | and_58_out | and_59_out | and_60_out | and_61_out | and_62_out | and_63_out | and_64_out | and_65_out;  // OR_Gate or_23, 4 bits wide
  Comparator #(.width(32)) comparator_29 (.a(RS2), .b({32{1'b0}}), .eq(rs2_is_0));  // open: gt, lt
  not not_2 (SPSel, push_or_pop);
  Comparator #(.width(3)) comparator_30 (.a(Instruction[14:12]), .b(3'b010), .eq(comparator_30_eq));  // open: gt, lt
  Comparator #(.width(7)) comparator_31 (.a(Instruction[6:0]), .b(7'b0100011), .eq(comparator_31_eq));  // open: gt, lt
  Comparator #(.width(7)) comparator_32 (.a(Instruction[6:0]), .b(7'b0110111), .eq(lui));  // open: gt, lt
  Comparator #(.width(7)) comparator_33 (.a(Instruction[6:0]), .b(7'b1101111), .eq(jal));  // open: gt, lt
  Comparator #(.width(3)) comparator_34 (.a(Instruction[14:12]), .b(3'b000), .eq(comparator_34_eq));  // open: gt, lt
  Comparator #(.width(7)) comparator_35 (.a(Instruction[6:0]), .b(7'b1100111), .eq(comparator_35_eq));  // open: gt, lt
  Comparator #(.width(3)) comparator_36 (.a(Instruction[14:12]), .b(3'b000), .eq(comparator_36_eq));  // open: gt, lt
  Comparator #(.width(3)) comparator_37 (.a(Instruction[14:12]), .b(3'b100), .eq(comparator_37_eq));  // open: gt, lt
  Comparator #(.width(3)) comparator_38 (.a(Instruction[14:12]), .b(3'b110), .eq(comparator_38_eq));  // open: gt, lt
  Comparator #(.width(3)) comparator_39 (.a(Instruction[14:12]), .b(3'b001), .eq(comparator_39_eq));  // open: gt, lt
  Comparator #(.width(7)) comparator_40 (.a(Instruction[6:0]), .b(7'b1100011), .eq(SB_Type));  // open: gt, lt
  and and_71 (sw, comparator_30_eq, comparator_31_eq);
  and and_72 (jalr, comparator_34_eq, comparator_35_eq);
  and and_73 (beq, SB_Type, comparator_36_eq);
  and and_74 (blt, SB_Type, comparator_37_eq);
  and and_75 (BrUn, SB_Type, comparator_38_eq);
  and and_76 (bne, SB_Type, comparator_39_eq);

  assign Funct3_load = Instruction[13:12];

  // Other names for the same wires on the sheet: bltu = BrUn; opcode[6:0] = Instruction[6:0];
  //   funct3[2:0] = Instruction[14:12]; funct7[6:0] = Instruction[31:25]; U_Type = lui

  // Notes on the sheet:
  //   Inputs
  //   Control Module
  //   R-Type
  //   Outputs
  //   I-Type
  //   Special Instructions
  //   S-Type
  //   U-Type
  //   UJ-Type
  //   jalr
  //   SB-Type
endmodule

module BranchComp (
  input  [31:0] br_r1,
  input  [31:0] br_r2,
  input  in_3,
  output BrEQ,
  output BrLT
);

  wire comparator_1_eq, comparator_1_lt, comparator_2_eq, comparator_2_lt;

  Comparator #(.width(32)) comparator_1 (.a(br_r1), .b(br_r2), .eq(comparator_1_eq), .lt(comparator_1_lt));  // open: gt
  Comparator #(.width(32), .mode("unsigned")) comparator_2 (
    .a(br_r1), .b(br_r2), .eq(comparator_2_eq), .lt(comparator_2_lt));  // open: gt
  Multiplexer #(.enable("false")) multiplexer_1 (.in0(comparator_1_eq), .in1(comparator_2_eq), .out(BrEQ), .sel(in_3));
  Multiplexer #(.enable("false")) multiplexer_2 (.in0(comparator_1_lt), .in1(comparator_2_lt), .out(BrLT), .sel(in_3));

  // Other names for the same wires on the sheet: BrUn = in_3

  // Notes on the sheet:
  //   Inputs
  //   Outputs
endmodule

module LoadGen (
  input  [31:0] Load_Bits,
  input  [31:0] ReadData,
  input  [1:0] LoadSel,
  output [31:0] Load_Result
);

  wire [7:0] multiplexer_1_out;
  wire [15:0] multiplexer_2_out;
  wire [31:0] bit_extender_1_out, bit_extender_2_out;

  Multiplexer #(.select(2), .width(8), .enable("false")) multiplexer_1 (
    .in0(ReadData[7:0]), .in1(ReadData[15:8]), .in2(ReadData[23:16]), .in3(ReadData[31:24]),
    .out(multiplexer_1_out), .sel(Load_Bits[1:0]));
  Multiplexer #(.select(2), .width(16), .enable("false")) multiplexer_2 (
    .in0(ReadData[15:0]), .in1(ReadData[15:0]), .in2(ReadData[31:16]), .in3(ReadData[31:16]),
    .out(multiplexer_2_out), .sel(Load_Bits[1:0]));
  assign bit_extender_1_out = {{24{multiplexer_1_out[7]}}, multiplexer_1_out};  // Bit_Extender bit_extender_1
  assign bit_extender_2_out = {{16{multiplexer_2_out[15]}}, multiplexer_2_out};  // Bit_Extender bit_extender_2
  Multiplexer #(.select(2), .width(32), .enable("false")) multiplexer_3 (
    .in0(bit_extender_1_out), .in1(bit_extender_2_out), .in2(ReadData), .in3(ReadData), .out(Load_Result),
    .sel(LoadSel));

  // Other names for the same wires on the sheet: Load_Bits_t[1:0] = Load_Bits[1:0]

  // Notes on the sheet:
  //   Inputs
  //   Output
endmodule
