// Logisim project alu.circ as structural Verilog: 2 circuits, main circuit alu
module alu (
  input  [31:0] A,
  input  [31:0] B,
  input  [3:0] ALUSel,
  output [31:0] Result
);

  wire comparator_1_lt;
  wire [5:0] bitadder_1_out, bitadder_2_out;
  wire [31:0] add, adder_3_out, and1, bit_extender_2_out, bit_extender_3_out, cnto, divu1, mulh1, mulhu1,
       mult1, multiplier_3_cout, multiplier_4_cout, multiplier_5_cout, multiplier_6_cout, or1, remu1, sll1,
       slt1, sra1, srl1, sub1, subtractor_2_out, subtractor_3_out, subtractor_4_out, xor1;

  Comparator #(.width(32)) comparator_1 (.a(A), .b(B), .lt(comparator_1_lt));  // open: gt, eq
  assign slt1 = {{31{1'b0}}, comparator_1_lt};  // Bit_Extender bit_extender_1
  // Probe on mulh1
  Adder #(.width(32)) adder_1 (.a(A), .b(B), .out(add));  // open: cin, cout
  assign and1 = A & B;  // AND_Gate and_1, 32 bits wide
  assign or1 = A | B;  // OR_Gate or_1, 32 bits wide
  assign xor1 = A ^ B;  // XOR_Gate xor_1, 32 bits wide
  Shifter #(.width(32), .shift("lr")) shifter_1 (.in(A), .\dist (B[4:0]), .out(srl1));
  Shifter #(.width(32), .shift("ar")) shifter_2 (.in(A), .\dist (B[4:0]), .out(sra1));
  Shifter #(.width(32)) shifter_3 (.in(A), .\dist (B[4:0]), .out(sll1));
  Divider #(.width(32)) divider_1 (.a(A), .b(B), .out(divu1));  // open: upper, rem
  Divider #(.width(32)) divider_2 (.a(A), .b(B), .rem(remu1));  // open: out, upper
  Multiplier #(.width(32)) multiplier_1 (.a(A), .b(B), .out(mult1));  // open: cin, cout
  Multiplier #(.width(32)) multiplier_2 (.a(A), .b(B), .cout(mulhu1));  // open: out, cin
  Subtractor #(.width(32)) subtractor_1 (.a(A), .b(B), .out(sub1));  // open: bin, bout
  BitAdder #(.width(32)) bitadder_1 (.in0(A), .out(bitadder_1_out));
  BitAdder #(.width(32)) bitadder_2 (.in0(B), .out(bitadder_2_out));
  assign bit_extender_2_out = {{26{1'b0}}, bitadder_1_out};  // Bit_Extender bit_extender_2
  assign bit_extender_3_out = {{26{1'b0}}, bitadder_2_out};  // Bit_Extender bit_extender_3
  Multiplexer #(.select(4), .width(32), .enable("false")) multiplexer_1 (
    .in0(add), .in1(and1), .in2(or1), .in3(xor1), .in4(srl1), .in5(sra1), .in6(sll1), .in7(slt1),
    .in8(divu1), .in9(remu1), .in10(mult1), .in11(mulhu1), .in12(sub1), .in13(cnto), .in14(mulh1),
    .out(Result), .sel(ALUSel));  // open: in15
  Adder #(.width(32)) adder_2 (.a(bit_extender_2_out), .b(bit_extender_3_out), .out(cnto));  // open: cin, cout
  // Probe on Result
  // Probe on ALUSel
  // Probe on Result
  Multiplier #(.width(32)) multiplier_3 (.a(B), .b(A), .cout(multiplier_3_cout));  // open: out, cin
  Adder #(.width(32)) adder_3 (.a(B), .b(A), .out(adder_3_out));  // open: cin, cout
  Multiplier #(.width(32)) multiplier_4 (.a(A), .b(B), .cout(multiplier_4_cout));  // open: out, cin
  Multiplier #(.width(32)) multiplier_5 (.a(A), .b(B), .cout(multiplier_5_cout));  // open: out, cin
  Subtractor #(.width(32)) subtractor_2 (.a(multiplier_5_cout), .b(A), .out(subtractor_2_out));  // open: bin, bout
  Subtractor #(.width(32)) subtractor_3 (.a(multiplier_3_cout), .b(B), .out(subtractor_3_out));  // open: bin, bout
  Multiplier #(.width(32)) multiplier_6 (.a(B), .b(A), .cout(multiplier_6_cout));  // open: out, cin
  Subtractor #(.width(32)) subtractor_4 (
    .a(multiplier_6_cout), .b(adder_3_out), .out(subtractor_4_out));  // open: bin, bout
  Multiplexer #(.select(2), .width(32), .enable("false")) multiplexer_2 (
    .in0(multiplier_4_cout), .in1(subtractor_2_out), .in2(subtractor_3_out), .in3(subtractor_4_out),
    .out(mulh1), .sel({A[31], B[31]}));
  // Probe on mulh1

  // Notes on the sheet:
  //   INPUTS to your circuit
  //   DON'T CHANGE THE LOCATIONS OF THE INPUTS AND OUTPUTS!
  //   OUTPUT from your circuit
endmodule

module mulh (
);

  wire [31:0] A, adder_1_out, adder_2_out, adder_3_out, adder_4_out, adder_5_out, adder_6_out, adder_7_out,
       B, mulhu1, multiplier_1_cout, multiplier_2_cout, multiplier_3_cout, multiplier_4_cout, negator_1_out,
       negator_2_out, negator_3_out, negator_4_out, negator_5_out, negator_6_out, negator_7_out;

  Negator #(.width(32)) negator_1 (.in(B), .out(negator_1_out));
  Negator #(.width(32)) negator_2 (.in(A), .out(negator_2_out));
  Negator #(.width(32)) negator_3 (.in(B), .out(negator_3_out));
  Negator #(.width(32)) negator_4 (.in(A), .out(negator_4_out));
  Adder #(.width(32)) adder_1 (.a(negator_1_out), .b(32'h1), .out(adder_1_out));  // open: cin, cout
  Multiplier #(.width(32)) multiplier_1 (.a(A), .b(B), .cout(multiplier_1_cout));  // open: out, cin
  Multiplier #(.width(32)) multiplier_2 (.a(A), .b(adder_1_out), .cout(multiplier_2_cout));  // open: out, cin
  Adder #(.width(32)) adder_2 (.a(negator_2_out), .b(32'h1), .out(adder_2_out));  // open: cin, cout
  Adder #(.width(32)) adder_3 (.a(negator_3_out), .b(32'h1), .out(adder_3_out));  // open: cin, cout
  Adder #(.width(32)) adder_4 (.a(negator_4_out), .b(32'h1), .out(adder_4_out));  // open: cin, cout
  Negator #(.width(32)) negator_5 (.in(multiplier_2_cout), .out(negator_5_out));
  Adder #(.width(32)) adder_5 (.a(negator_5_out), .b(32'h1), .out(adder_5_out));  // open: cin, cout
  Negator #(.width(32)) negator_6 (.in(multiplier_3_cout), .out(negator_6_out));
  Multiplier #(.width(32)) multiplier_3 (.a(B), .b(adder_2_out), .cout(multiplier_3_cout));  // open: out, cin
  Adder #(.width(32)) adder_6 (.a(negator_6_out), .b(32'h1), .out(adder_6_out));  // open: cin, cout
  Multiplier #(.width(32)) multiplier_4 (.a(adder_3_out), .b(adder_4_out), .cout(multiplier_4_cout));  // open: out, cin
  Multiplexer #(.select(2), .width(32), .enable("false")) multiplexer_1 (
    .in0(multiplier_1_cout), .in1(adder_5_out), .in2(adder_6_out), .in3(adder_7_out), .out(mulhu1),
    .sel({B[31], A[31]}));
  Adder #(.width(32)) adder_7 (.a(negator_7_out), .b(32'h1), .out(adder_7_out));  // open: cin, cout
  Negator #(.width(32)) negator_7 (.in(multiplier_4_cout), .out(negator_7_out));
endmodule
