// Logisim project cpu.circ as structural Verilog: 4 circuits, main circuit main
module main (
  input  [31:0] INSTRUCTION,
  input  CLOCK,
  output [31:0] ra,
  output [31:0] sp,
  output [31:0] t0,
  output [31:0] t1,
  output [31:0] t2,
  output [31:0] s0,
  output [31:0] s1,
  output [31:0] a0,
  output [31:0] FETCH_ADDRESS
);

  wire branchcomp_1_breq, branchcomp_1_brlt, controllogic_1_asel, controllogic_1_brun, controllogic_1_bsel,
       controllogic_1_memrw, controllogic_1_pcsel, controllogic_1_regwen;
  wire [1:0] controllogic_1_wbsel;
  wire [2:0] controllogic_1_immsel;
  wire [3:0] controllogic_1_alusel;
  wire [4:0] rd, rs1, rs2;
  wire [31:0] adder_1_out, Arithmetic_Logic_Unit_result, DMEM_p5, immgen_1_immgen031, instD_q,
       multiplexer_1_out, multiplexer_2_out, multiplexer_3_out, multiplexer_4_out, multiplexer_5_out, pcD_q,
       RegFile_read_data_1, RegFile_read_data_2;

  Adder #(.width(32)) adder_1 (.a(FETCH_ADDRESS), .b(32'h1), .out(adder_1_out));  // open: cin, cout
  Multiplexer #(.width(32), .enable("false")) multiplexer_1 (
    .in0(adder_1_out), .in1(Arithmetic_Logic_Unit_result), .out(multiplexer_1_out), .sel(controllogic_1_pcsel));
  // Probe on multiplexer_1_out
  // Probe on INSTRUCTION
  Register #(.width(32)) instD (
    .D(multiplexer_2_out), .clk(CLOCK), .Q({instD_q[31:25], rs2, rs1, instD_q[14:12], rd, instD_q[6:0]}));  // open: en, clr
  Register #(.width(32)) PC (.D(multiplexer_1_out), .clk(CLOCK), .Q(FETCH_ADDRESS));  // open: en, clr
  // Probe on rd
  Multiplexer #(.width(32), .enable("false")) multiplexer_2 (
    .in0(INSTRUCTION), .in1(32'h13), .out(multiplexer_2_out), .sel(controllogic_1_pcsel));
  // Probe on controllogic_1_pcsel
  // Probe on rs1
  // Probe on rs2
  // Probe on {instD_q[31:25], rs2, rs1, instD_q[14:12], rd, instD_q[6:0]}
  // Probe on multiplexer_2_out
  Register #(.width(32)) pcD (.D(FETCH_ADDRESS), .clk(CLOCK), .Q(pcD_q));  // open: en, clr
  // Probe on multiplexer_5_out
  Controllogic controllogic_1 (
    .INSTRUCTION({instD_q[31:25], rs2, rs1, instD_q[14:12], rd, instD_q[6:0]}), .BrEq(branchcomp_1_breq),
    .BrLT(branchcomp_1_brlt), .RegWEn(controllogic_1_regwen), .ALUSel(controllogic_1_alusel),
    .MemRW(controllogic_1_memrw), .BSel(controllogic_1_bsel), .WBSel(controllogic_1_wbsel),
    .ASel(controllogic_1_asel), .ImmSel(controllogic_1_immsel), .BrUn(controllogic_1_brun),
    .PCSel(controllogic_1_pcsel));
  regfile_main RegFile (
    .rs2(rs2), .rd(rd), .Read_Data_1(RegFile_read_data_1), .Read_Data_2(RegFile_read_data_2), .ra(ra),
    .sp(sp), .t0(t0), .t1(t1), .t2(t2), .s0(s0), .s1(s1), .a0(a0), .rs1(rs1), .Write_Data(multiplexer_5_out),
    .RegWEn(controllogic_1_regwen), .clk(CLOCK));
  ImmGen immgen_1 (
    .ImmSel(controllogic_1_immsel),
    .Instruction({instD_q[31:25], rs2, rs1, instD_q[14:12], rd, instD_q[6:0]}), .ImmGen031(immgen_1_immgen031));
  BranchComp branchcomp_1 (
    .DataA(RegFile_read_data_1), .DataB(RegFile_read_data_2), .BrUn(controllogic_1_brun),
    .BrEq(branchcomp_1_breq), .BrLT(branchcomp_1_brlt));
  // Probe on immgen_1_immgen031
  Multiplexer #(.width(32), .enable("false")) multiplexer_3 (
    .in0(RegFile_read_data_1), .in1(pcD_q), .out(multiplexer_3_out), .sel(controllogic_1_asel));
  Multiplexer #(.width(32), .enable("false")) multiplexer_4 (
    .in0(RegFile_read_data_2), .in1(immgen_1_immgen031), .out(multiplexer_4_out), .sel(controllogic_1_bsel));
  alu Arithmetic_Logic_Unit (
    .A(multiplexer_3_out), .B(multiplexer_4_out), .ALUSel(controllogic_1_alusel),
    .Result(Arithmetic_Logic_Unit_result));
  // Probe on controllogic_1_wbsel
  // Probe on Arithmetic_Logic_Unit_result
  // Probe on controllogic_1_memrw
  // mem_main DMEM: pin names not known; wires that end beside it: Arithmetic_Logic_Unit_result, RegFile_read_data_2, controllogic_1_memrw, CLOCK, DMEM_p5
  Multiplexer #(.select(2), .width(32), .enable("false")) multiplexer_5 (
    .in0(DMEM_p5), .in1(Arithmetic_Logic_Unit_result), .in2(adder_1_out), .out(multiplexer_5_out),
    .sel(controllogic_1_wbsel));  // open: in3

  // Other names for the same wires on the sheet: clk = CLOCK; fetch_addr[31:0] = FETCH_ADDRESS

  // Notes on the sheet:
  //   Output
  //   NOP
  //   Inputs/Outputs from run.circ. DO NOT MOVE THESE.
  //   Inputs
  //   Inputs/Outputs from run.circ. DO NOT MOVE THESE.
endmodule

module Controllogic (
  input  [31:0] INSTRUCTION,
  input  BrEq,
  input  BrLT,
  output RegWEn,
  output [3:0] ALUSel,
  output MemRW,
  output BSel,
  output [1:0] WBSel,
  output ASel,
  output [2:0] ImmSel,
  output BrUn,
  output PCSel
);

  wire add, addi, and1, and_1_out, and_2_out, and_3_out, and_4_out, and_5_out, and_6_out, and_7_out,
       and_8_out, and_9_out, and_10_out, and_11_out, and_12_out, and_26_out, and_27_out, andi, beq, blt,
       bltu, bne, comparator_2_eq, comparator_3_eq, comparator_4_eq, comparator_5_eq, comparator_6_eq,
       comparator_7_eq, comparator_8_eq, comparator_9_eq, comparator_10_eq, comparator_11_eq,
       comparator_12_eq, comparator_13_eq, comparator_14_eq, comparator_15_eq, comparator_16_eq,
       comparator_17_eq, comparator_18_eq, comparator_19_eq, comparator_20_eq, comparator_21_eq,
       comparator_22_eq, comparator_23_eq, comparator_24_eq, comparator_26_eq, comparator_28_eq,
       comparator_29_eq, comparator_30_eq, comparator_31_eq, divu, I_type, jal, jalr, lb, lh, lui, lw, mul,
       mulh, mulhu, not_1_out, not_2_out, or1, or_4_out, or_5_out, or_6_out, or_13_out, or_14_out, or_15_out,
       or_16_out, or_17_out, or_18_out, or_19_out, ori, R_type, remu, SB_type, sll1, slli, slt, slti, srai,
       srl1, srli, sub, sw, xor1, xori;
  wire [1:0] and_40_out, and_41_out, bit_extender_1_out, bit_extender_2_out, bit_extender_3_out;
  wire [2:0] or_2_out;
  wire [3:0] and_47_out, and_48_out, and_49_out, and_50_out, and_51_out, and_52_out, and_53_out, and_54_out,
       and_55_out, and_56_out, and_57_out, and_58_out, and_59_out, and_60_out, bit_extender_4_out,
       bit_extender_5_out, bit_extender_6_out, bit_extender_7_out, bit_extender_8_out, bit_extender_9_out,
       bit_extender_10_out, bit_extender_11_out, bit_extender_12_out, bit_extender_13_out,
       bit_extender_14_out, bit_extender_15_out, bit_extender_16_out, bit_extender_17_out;

  and and_1 (and_1_out, beq, BrEq);
  and and_2 (and_2_out, bne, not_1_out);
  not not_1 (not_1_out, BrEq);
  Comparator #(.width(7)) comparator_1 (.a(INSTRUCTION[6:0]), .b(7'b0110011), .eq(R_type));  // open: gt, lt
  Comparator #(.width(3)) comparator_2 (.a(INSTRUCTION[14:12]), .b(3'b000), .eq(comparator_2_eq));  // open: gt, lt
  Comparator #(.width(3)) comparator_3 (.a(INSTRUCTION[14:12]), .b(3'b001), .eq(comparator_3_eq));  // open: gt, lt
  Comparator #(.width(3)) comparator_4 (.a(INSTRUCTION[14:12]), .b(3'b010), .eq(comparator_4_eq));  // open: gt, lt
  Comparator #(.width(3)) comparator_5 (.a(INSTRUCTION[14:12]), .b(3'b011), .eq(comparator_5_eq));  // open: gt, lt
  Comparator #(.width(3)) comparator_6 (.a(INSTRUCTION[14:12]), .b(3'b100), .eq(comparator_6_eq));  // open: gt, lt
  Comparator #(.width(3)) comparator_7 (.a(INSTRUCTION[14:12]), .b(3'b101), .eq(comparator_7_eq));  // open: gt, lt
  Comparator #(.width(3)) comparator_8 (.a(INSTRUCTION[14:12]), .b(3'b110), .eq(comparator_8_eq));  // open: gt, lt
  Comparator #(.width(3)) comparator_9 (.a(INSTRUCTION[14:12]), .b(3'b111), .eq(comparator_9_eq));  // open: gt, lt
  and and_3 (and_3_out, blt, BrLT);
  and and_4 (and_4_out, bltu, BrLT);
  or or_1 (PCSel, and_1_out, and_2_out, and_3_out, and_4_out, jalr, jal);
  // Probe on PCSel
  // Probe on INSTRUCTION[6:0]
  and and_5 (and_5_out, R_type, comparator_3_eq);
  and and_6 (and_6_out, R_type, comparator_4_eq);
  and and_7 (and_7_out, R_type, comparator_5_eq);
  and and_8 (and_8_out, R_type, comparator_6_eq);
  and and_9 (and_9_out, R_type, comparator_7_eq);
  and and_10 (and_10_out, R_type, comparator_8_eq);
  and and_11 (and_11_out, R_type, comparator_9_eq);
  and and_12 (and_12_out, R_type, comparator_2_eq);
  Comparator #(.width(7)) comparator_10 (.a(INSTRUCTION[31:25]), .b({7{1'b0}}), .eq(comparator_10_eq));  // open: gt, lt
  Comparator #(.width(7)) comparator_11 (
    .a(INSTRUCTION[31:25]), .b(7'b0000001), .eq(comparator_11_eq));  // open: gt, lt
  Comparator #(.width(7)) comparator_12 (
    .a(INSTRUCTION[31:25]), .b(7'b0100000), .eq(comparator_12_eq));  // open: gt, lt
  and and_13 (add, and_12_out, comparator_10_eq);
  and and_14 (mul, and_12_out, comparator_11_eq);
  and and_15 (sub, and_12_out, comparator_12_eq);
  and and_16 (sll1, and_5_out, comparator_10_eq);
  and and_17 (mulh, and_5_out, comparator_11_eq);
  and and_18 (slt, comparator_10_eq, and_6_out);
  and and_19 (mulhu, comparator_11_eq, and_7_out);
  and and_20 (xor1, comparator_10_eq, and_8_out);
  and and_21 (divu, comparator_11_eq, and_9_out);
  and and_22 (srl1, comparator_10_eq, and_9_out);
  and and_23 (or1, comparator_10_eq, and_10_out);
  and and_24 (remu, comparator_11_eq, and_11_out);
  and and_25 (and1, comparator_10_eq, and_11_out);
  or or_2 (or_2_out[0], lb, lh, lw, addi, slli, slti, xori, srli, srai, ori, andi, jalr);
  or or_3 (or_2_out[2], beq, blt, bltu, bne);
  // Probe on {jal, lui, or_2_out[2], sw, or_2_out[0]}
  // Probe on comparator_14_eq
  Multiplexer #(.select(5), .width(3), .enable("false")) multiplexer_1 (
    .in1(3'b000), .in2(3'b001), .in4(3'b010), .in8(3'b011), .in16(3'b100), .out(ImmSel),
    .sel({jal, lui, or_2_out[2], sw, or_2_out[0]}));  // open: in0, in3, in5, in6, in7, in9, in10, in11, in12, in13, in14, in15, in17, in18, in19, in20, in21, in22, in23, in24, in25, in26, in27, in28, in29, in30, in31
  Comparator #(.width(7), .mode("unsigned")) comparator_13 (
    .a(INSTRUCTION[6:0]), .b(7'b0000011), .eq(comparator_13_eq));  // open: gt, lt
  Comparator #(.width(7)) comparator_14 (.a(INSTRUCTION[6:0]), .b(7'b0010011), .eq(comparator_14_eq));  // open: gt, lt
  Comparator #(.width(3)) comparator_15 (.a(INSTRUCTION[14:12]), .b(3'b000), .eq(comparator_15_eq));  // open: gt, lt
  Comparator #(.width(3)) comparator_16 (.a(INSTRUCTION[14:12]), .b(3'b001), .eq(comparator_16_eq));  // open: gt, lt
  Comparator #(.width(3)) comparator_17 (.a(INSTRUCTION[14:12]), .b(3'b010), .eq(comparator_17_eq));  // open: gt, lt
  Comparator #(.width(3)) comparator_18 (.a(INSTRUCTION[14:12]), .b(3'b100), .eq(comparator_18_eq));  // open: gt, lt
  Comparator #(.width(3)) comparator_19 (.a(INSTRUCTION[14:12]), .b(3'b101), .eq(comparator_19_eq));  // open: gt, lt
  Comparator #(.width(3)) comparator_20 (.a(INSTRUCTION[14:12]), .b(3'b110), .eq(comparator_20_eq));  // open: gt, lt
  Comparator #(.width(3)) comparator_21 (.a(INSTRUCTION[14:12]), .b(3'b111), .eq(comparator_21_eq));  // open: gt, lt
  Comparator #(.width(7)) comparator_22 (.a(INSTRUCTION[31:25]), .b({7{1'b0}}), .eq(comparator_22_eq));  // open: gt, lt
  Comparator #(.width(7)) comparator_23 (
    .a(INSTRUCTION[31:25]), .b(7'b0100000), .eq(comparator_23_eq));  // open: gt, lt
  Comparator #(.width(7)) comparator_24 (.a(INSTRUCTION[6:0]), .b(7'b1100111), .eq(comparator_24_eq));  // open: gt, lt
  // Probe on ImmSel
  or or_4 (or_4_out, R_type, lui, addi, slli, slti, xori, srli, srai, ori, andi);
  or or_5 (or_5_out, lb, lh, lw);
  or or_6 (or_6_out, jalr, jal);
  or or_7 (I_type, comparator_13_eq, comparator_14_eq, comparator_24_eq);
  and and_26 (and_26_out, comparator_14_eq, comparator_16_eq);
  and and_27 (and_27_out, comparator_14_eq, comparator_19_eq);
  // Probe on or_4_out
  assign bit_extender_1_out = {{1{1'b0}}, or_4_out};  // Bit_Extender bit_extender_1
  assign bit_extender_2_out = {{1{or_5_out}}, or_5_out};  // Bit_Extender bit_extender_2
  assign bit_extender_3_out = {{1{or_6_out}}, or_6_out};  // Bit_Extender bit_extender_3
  and and_28 (lb, comparator_13_eq, comparator_15_eq);
  and and_29 (lh, comparator_13_eq, comparator_16_eq);
  and and_30 (lw, comparator_13_eq, comparator_17_eq);
  and and_31 (addi, comparator_14_eq, comparator_15_eq);
  and and_32 (slli, and_26_out, comparator_22_eq);
  and and_33 (slti, comparator_14_eq, comparator_17_eq);
  and and_34 (xori, comparator_14_eq, comparator_18_eq);
  and and_35 (srli, and_27_out, comparator_22_eq);
  and and_36 (srai, and_27_out, comparator_23_eq);
  and and_37 (ori, comparator_14_eq, comparator_20_eq);
  and and_38 (andi, comparator_14_eq, comparator_21_eq);
  and and_39 (jalr, comparator_15_eq, comparator_24_eq);
  assign and_40_out = bit_extender_2_out & 2'b00;  // AND_Gate and_40, 2 bits wide
  assign and_41_out = bit_extender_3_out & 2'b10;  // AND_Gate and_41, 2 bits wide
  or or_8 (ASel, jal, SB_type);
  or or_9 (BSel, I_type, MemRW, SB_type, lui, jal);
  // Probe on BSel
  or or_10 (RegWEn, I_type, R_type, lui, jal);
  // Probe on WBSel
  assign WBSel = bit_extender_1_out | and_40_out | and_41_out;  // OR_Gate or_11, 2 bits wide
  not not_2 (not_2_out, blt);
  Comparator #(.width(7)) comparator_25 (.a(INSTRUCTION[6:0]), .b(7'b0100011), .eq(MemRW));  // open: gt, lt
  Comparator #(.width(3)) comparator_26 (.a(INSTRUCTION[14:12]), .b(3'b010), .eq(comparator_26_eq));  // open: gt, lt
  Comparator #(.width(7)) comparator_27 (.a(INSTRUCTION[6:0]), .b(7'b1100011), .eq(SB_type));  // open: gt, lt
  Comparator #(.width(3)) comparator_28 (.a(INSTRUCTION[14:12]), .b(3'b000), .eq(comparator_28_eq));  // open: gt, lt
  Comparator #(.width(3)) comparator_29 (.a(INSTRUCTION[14:12]), .b(3'b100), .eq(comparator_29_eq));  // open: gt, lt
  Comparator #(.width(3)) comparator_30 (.a(INSTRUCTION[14:12]), .b(3'b110), .eq(comparator_30_eq));  // open: gt, lt
  Comparator #(.width(3)) comparator_31 (.a(INSTRUCTION[14:12]), .b(3'b001), .eq(comparator_31_eq));  // open: gt, lt
  Comparator #(.width(7)) comparator_32 (.a(INSTRUCTION[6:0]), .b(7'b0110111), .eq(lui));  // open: gt, lt
  Comparator #(.width(7)) comparator_33 (.a(INSTRUCTION[6:0]), .b(7'b1101111), .eq(jal));  // open: gt, lt
  or or_12 (BrUn, not_2_out, bltu);
  and and_42 (sw, MemRW, comparator_26_eq);
  // Probe on BrUn
  and and_43 (beq, SB_type, comparator_28_eq);
  and and_44 (blt, SB_type, comparator_29_eq);
  and and_45 (bltu, SB_type, comparator_30_eq);
  and and_46 (bne, SB_type, comparator_31_eq);
  or or_13 (or_13_out, and1, andi);
  or or_14 (or_14_out, or1, ori);
  or or_15 (or_15_out, xor1, xori);
  or or_16 (or_16_out, srl1, srli);
  or or_17 (or_17_out, sll1, slli);
  or or_18 (or_18_out, slt, slti);
  or or_19 (or_19_out, jalr, lb, lh, lw, addi, add, MemRW, SB_type, lui, jal);
  assign bit_extender_4_out = {{3{mulhu}}, mulhu};  // Bit_Extender bit_extender_4
  assign bit_extender_5_out = {{3{sub}}, sub};  // Bit_Extender bit_extender_5
  assign bit_extender_6_out = {{3{mulh}}, mulh};  // Bit_Extender bit_extender_6
  assign bit_extender_7_out = {{3{or_19_out}}, or_19_out};  // Bit_Extender bit_extender_7
  assign bit_extender_8_out = {{3{or_13_out}}, or_13_out};  // Bit_Extender bit_extender_8
  assign bit_extender_9_out = {{3{or_14_out}}, or_14_out};  // Bit_Extender bit_extender_9
  assign bit_extender_10_out = {{3{or_15_out}}, or_15_out};  // Bit_Extender bit_extender_10
  assign bit_extender_11_out = {{3{or_16_out}}, or_16_out};  // Bit_Extender bit_extender_11
  assign bit_extender_12_out = {{3{srai}}, srai};  // Bit_Extender bit_extender_12
  assign bit_extender_13_out = {{3{or_17_out}}, or_17_out};  // Bit_Extender bit_extender_13
  assign bit_extender_14_out = {{3{or_18_out}}, or_18_out};  // Bit_Extender bit_extender_14
  assign bit_extender_15_out = {{3{divu}}, divu};  // Bit_Extender bit_extender_15
  assign bit_extender_16_out = {{3{remu}}, remu};  // Bit_Extender bit_extender_16
  assign bit_extender_17_out = {{3{mul}}, mul};  // Bit_Extender bit_extender_17
  assign and_47_out = bit_extender_7_out & 4'b0000;  // AND_Gate and_47, 4 bits wide
  assign and_48_out = bit_extender_8_out & 4'b0001;  // AND_Gate and_48, 4 bits wide
  assign and_49_out = bit_extender_9_out & 4'b0010;  // AND_Gate and_49, 4 bits wide
  assign and_50_out = bit_extender_10_out & 4'b0011;  // AND_Gate and_50, 4 bits wide
  assign and_51_out = bit_extender_11_out & 4'b0100;  // AND_Gate and_51, 4 bits wide
  assign and_52_out = bit_extender_12_out & 4'b0101;  // AND_Gate and_52, 4 bits wide
  assign and_53_out = bit_extender_13_out & 4'b0110;  // AND_Gate and_53, 4 bits wide
  assign and_54_out = bit_extender_14_out & 4'b0111;  // AND_Gate and_54, 4 bits wide
  assign and_55_out = bit_extender_15_out & 4'b1000;  // AND_Gate and_55, 4 bits wide
  assign and_56_out = bit_extender_16_out & 4'b1001;  // AND_Gate and_56, 4 bits wide
  assign and_57_out = bit_extender_17_out & 4'b1010;  // AND_Gate and_57, 4 bits wide
  assign and_58_out = bit_extender_4_out & 4'b1011;  // AND_Gate and_58, 4 bits wide
  assign and_59_out = bit_extender_5_out & 4'b1100;  // AND_Gate and_59, 4 bits wide
  assign and_60_out = bit_extender_6_out & 4'b1110;  // AND_Gate and_60, 4 bits wide
  // Probe on and_47_out
  // Probe on ALUSel
  assign ALUSel = and_47_out | and_48_out | and_49_out | and_50_out | and_51_out | and_52_out | and_53_out | and_54_out | and_55_out | and_56_out | and_57_out | and_58_out | and_59_out | and_60_out;  // OR_Gate or_20, 4 bits wide

  // Other names for the same wires on the sheet: U_type = lui; UJ_type = jal; Opcode[6:0] = INSTRUCTION[6:0];
  //   funct3[2:0] = INSTRUCTION[14:12]; funct7[6:0] = INSTRUCTION[31:25]; S_type = MemRW

  // Notes on the sheet:
  //   R-type Instructions
  //   compare opcode
  //   compare funct3
  //   compare funct7
  //   compare opcode
  //   compare funct3
  //   compare funct7
  //   I-type Instructions
  //   compare opcode
  //   compare funct3
  //   compare opcode
  //   compare funct3
  //   compare opcode
  //   compare opcode
  //   S-type Instruction
  //   SB-type Instructions
  //   U-type Instruction
  //   UJ-type Instruction
endmodule

module ImmGen (
  input  [2:0] ImmSel,
  input  [31:0] Instruction,
  output [31:0] ImmGen031
);

  wire comparator_1_eq;
  wire [11:0] bit_extender_4_out;
  wire [19:0] bit_extender_3_out;
  wire [20:0] bit_extender_1_out;
  wire [31:0] B_Format, I_Format, J_Format, shifter_1_out;
  wire [31:11] S_Format;

  assign bit_extender_1_out = {{20{Instruction[31]}}, Instruction[31]};  // Bit_Extender bit_extender_1
  Comparator #(.width(7)) comparator_1 (.a(Instruction[6:0]), .b(7'b1100111), .eq(comparator_1_eq));  // open: gt, lt
  assign S_Format = {{20{Instruction[31]}}, Instruction[31]};  // Bit_Extender bit_extender_2
  Shifter #(.width(32), .shift("ar")) shifter_1 (
    .in({bit_extender_1_out, Instruction[30:20]}), .\dist (5'b00010), .out(shifter_1_out));
  assign bit_extender_3_out = {{19{Instruction[31]}}, Instruction[31]};  // Bit_Extender bit_extender_3
  assign bit_extender_4_out = {{11{Instruction[31]}}, Instruction[31]};  // Bit_Extender bit_extender_4
  Multiplexer #(.width(32), .enable("false")) multiplexer_1 (
    .in0({bit_extender_1_out, Instruction[30:20]}), .in1(shifter_1_out), .out(I_Format), .sel(comparator_1_eq));
  // Probe on comparator_1_eq
  // Probe on {bit_extender_3_out, Instruction[7], Instruction[30:25], Instruction[11:8], 1'b0}
  // Probe on {bit_extender_4_out, Instruction[19:12], Instruction[20], Instruction[30:21], 1'b0}
  Shifter #(.width(32), .shift("ar")) shifter_2 (
    .in({bit_extender_3_out, Instruction[7], Instruction[30:25], Instruction[11:8], 1'b0}),
    .\dist (5'b00010), .out(B_Format));
  // Probe on B_Format
  Shifter #(.width(32), .shift("ar")) shifter_3 (
    .in({bit_extender_4_out, Instruction[19:12], Instruction[20], Instruction[30:21], 1'b0}),
    .\dist (5'b00010), .out(J_Format));
  // Probe on J_Format
  Multiplexer #(.select(3), .width(32), .enable("false")) multiplexer_2 (
    .in0(I_Format), .in1({S_Format, Instruction[30:25], Instruction[11:7]}), .in2(B_Format),
    .in3({Instruction[31:12], {12{1'b0}}}), .in4(J_Format), .out(ImmGen031), .sel(ImmSel));  // open: in5, in6, in7
  // Probe on ImmGen031

  // Other names for the same wires on the sheet: S_Format[10:0] = {Instruction[30:25], Instruction[11:7]};
  //   U_Format[31:12] = Instruction[31:12]; Imm_out[31:0] = ImmGen031
endmodule

module BranchComp (
  input  [31:0] DataA,
  input  [31:0] DataB,
  input  BrUn,
  output BrEq,
  output BrLT
);

  wire comparator_1_eq, comparator_1_lt, comparator_2_eq, comparator_2_lt;

  Comparator #(.width(32)) comparator_1 (.a(DataA), .b(DataB), .eq(comparator_1_eq), .lt(comparator_1_lt));  // open: gt
  Comparator #(.width(32), .mode("unsigned")) comparator_2 (
    .a(DataA), .b(DataB), .eq(comparator_2_eq), .lt(comparator_2_lt));  // open: gt
  // Probe on BrUn
  Multiplexer #(.enable("false")) multiplexer_1 (.in0(comparator_1_eq), .in1(comparator_2_eq), .out(BrEq), .sel(BrUn));
  Multiplexer #(.enable("false")) multiplexer_2 (.in0(comparator_1_lt), .in1(comparator_2_lt), .out(BrLT), .sel(BrUn));

  // Other names for the same wires on the sheet: A[31:0] = DataA; B[31:0] = DataB
endmodule
